# Fritzing sketch ColorButton (saved by Fritzing 0.9.3b)
breadboards: 1

parts:
  LED1 = RGB LED (com. cathode, rbg) [package="5 mm [THT]"]
  S1 = Momentary Switch [package=ksa_sealed_tac_switch]
  S2 = Momentary Switch [package=ksa_sealed_tac_switch]
  S3 = Momentary Switch [package=ksa_sealed_tac_switch]
  R1 = Resistor [tolerance=±5% resistance=10k package="2512 [SMD]"]
  R2 = Resistor [tolerance=±5% resistance=10k package="2512 [SMD]"]
  R3 = Resistor [tolerance=±5% resistance=10k package="2512 [SMD]"]
  R4 = Resistor [tolerance=±1% resistance=220 package="2512 [SMD]"]
  Componente1 = Arduino Uno (Rev3)

nets:
  N1: LED1.red_anode, Componente1.D9_PWM
  N2: LED1.common_cathode, R4.Pin_0
  N3: LED1.blue_anode, Componente1.D10_PWM/SS
  N4: LED1.green_anode, Componente1.D11_PWM/MOSI
  N5: S1.1, Componente1.D2
  N6: S1.2, R3.Pin_0
  N7: S1.4, S2.4, S3.4, Componente1.5V
  N8: S2.1, Componente1.D3_PWM
  N9: S2.2, R1.Pin_0
  N10: S3.1, Componente1.D4
  N11: S3.2, R2.Pin_0
  N12: R1.Pin_1, R2.Pin_1, R3.Pin_1, R4.Pin_1, Componente1.GND
