# Fritzing sketch ColorTryAll (saved by Fritzing 0.9.3b)
circuit board: 13.7095cm x 8.10314cm
breadboards: 1

parts:
  RGB_Led = RGB LED (com. cathode, rbg) [package="5 mm [THT]"]
  Arduino_UNO = Arduino Uno (Rev3)
  R1 = Resistor [tolerance=±1% resistance=220 package="0402 [SMD]"]

nets (from the breadboard view):
  N1: RGB_Led.red_anode, Arduino_UNO.D9_PWM
  N2: RGB_Led.common_cathode, R1.Pin_0
  N3: RGB_Led.blue_anode, Arduino_UNO.D11_PWM/MOSI
  N4: RGB_Led.green_anode, Arduino_UNO.D10_PWM/SS
  N5: Arduino_UNO.GND, R1.Pin_1
